// Digital circuit memory.dig as structural Verilog
// 数据存储器
module memory (
  input  clk,
  input  rst,
  input  [3:0] op,
  input  [31:0] din,
  input  [31:0] address,
  output [31:0] dout
);

  wire [31:0] bitextender_1_out, bitextender_2_out, multiplexer_1_out, multiplexer_2_out, multiplexer_3_out,
       ramdualport_1_d;

  Multiplexer #(.Bits(32), .Selector_Bits(2)) multiplexer_1 (
    .sel(op[1:0]), .in_0({{24{1'b0}}, din[7:0]}), .in_1({{16{1'b0}}, din[15:0]}), .in_2(din),
    .in_3({32{1'b0}}), .out(multiplexer_1_out));
  RAMDualPort #(.AddrBits(20), .Bits(32)) ramdualport_1 (
    .A(address[21:2]), .Din(multiplexer_1_out), .str(op[3]), .C(clk), .ld(1'b1), .D(ramdualport_1_d));
  BitExtender #(.outputBits(32)) bitextender_1 (.in(ramdualport_1_d[7:0]), .out(bitextender_1_out));
  BitExtender #(.inputBits(16), .outputBits(32)) bitextender_2 (.in(ramdualport_1_d[15:0]), .out(bitextender_2_out));
  Multiplexer #(.Selector_Bits(2), .Bits(32)) multiplexer_2 (
    .sel(op[1:0]), .in_0(bitextender_1_out), .in_1(bitextender_2_out), .in_2(ramdualport_1_d),
    .in_3({32{1'b0}}), .out(multiplexer_2_out));
  Multiplexer #(.Bits(32)) multiplexer_3 (
    .sel(op[2]), .in_0(multiplexer_2_out), .in_1(ramdualport_1_d), .out(multiplexer_3_out));
  Multiplexer #(.Bits(32)) multiplexer_4 (.sel(rst), .in_0(multiplexer_3_out), .in_1({32{1'b0}}), .out(dout));

  // Notes on the sheet:
  //   op: 操作码
  //   din: 输入
  //   dout: 输出
endmodule
